# Fritzing sketch 1 (saved by Fritzing 0.9.4)
breadboards: 1

parts:
  Power_plug1 = Power plug
  IC1 = IC, DIP package, 14 pins [chip_label="IC 7400"]
  R1 = Trimmer Potentiometer [maximum_resistance=10kΩ package=THT]
  R2 = Resistor [tolerance=±5% resistance=220 package=THT]

nets:
  N1: Power_plug1.GND, IC1.pin7, R1.leg1
  N2: Power_plug1.VCC, IC1.pin14, R1.leg2, R2.Pin_0
  N3: IC1.pin1, R2.Pin_1
  N4: IC1.pin2, R1.wiper

notes:
  SCOPE INPUT
