# Fritzing sketch 2 (saved by Fritzing 0.9.4)
breadboards: 2

parts:
  Power_plug1 = Power plug
  IC1 = IC, DIP package, 14 pins [chip_label="IC 7400"]
  R1 = Trimmer Potentiometer [maximum_resistance=10kΩ package=THT]
  R2 = Resistor [tolerance=±5% resistance=220 package=THT]
  IC2 = IC, DIP package, 14 pins [chip_label="IC 7400"]
  IC3 = IC, DIP package, 14 pins [chip_label="IC 7400"]

nets:
  N1: Power_plug1.GND, IC1.pin7, R1.leg1, IC2.pin7, IC3.pin7
  N2: Power_plug1.VCC, IC1.pin14, R1.leg2, R2.Pin_0, IC2.pin14, IC3.pin14
  N3: IC1.pin1, IC1.pin5, IC1.pin10, IC1.pin13, R2.Pin_1, IC2.pin2, IC2.pin5, IC2.pin10, IC2.pin13, IC3.pin2, IC3.pin5, IC3.pin13
  N4: IC1.pin2, R1.wiper
  N5: IC1.pin3, IC1.pin4, IC1.pin9, IC1.pin12, IC2.pin1, IC2.pin4, IC2.pin9, IC2.pin12, IC3.pin1, IC3.pin4, IC3.pin12

notes:
  SCOPE INPUT
