# Fritzing sketch d (saved by Fritzing 0.9.4)
breadboards: 1

parts:
  Power_plug1 = Power plug
  U1 = 555 Timer [package="DIP8 [THT]"]
  C1 = Capacitor [package=cap-pth-small]
  C2 = Capacitor [package=cap-pth-small]
  R1 = 12 kΩ Resistor [package=THT]
  R2 = 1.5 kΩ Resistor [package=THT]
  U2 = 74HC04_HEX_INVERTER [package=dil14]

nets:
  GND: Power_plug1.GND, U1.Ground, C1.1, C2.2, U2.GND
  VCC: Power_plug1.VCC, U1.Reset, U1.Vcc_Supply_Voltage, R1.Pin_1, U2.VCC
  N1: U1.Trigger, U1.Threshold, C1.2, R2.Pin_0
  N2: U1.Output, U2.1A
  N3: U1.Control_Voltage, C2.1
  N4: U1.Discharge, R1.Pin_0, R2.Pin_1

custom parts:
  12 kΩ Resistor: A generic resistor (0.25W)
  1.5 kΩ Resistor: A generic resistor (0.25W)
