# Fritzing sketch d (saved by Fritzing 0.9.4)
breadboards: 2

parts:
  Power_plug1 = Power plug
  S1 = Pushbutton [package="[THT]"]
  S2 = Pushbutton [package="[THT]"]
  R1 = Resistor [tolerance=±5% resistance=220 package=THT]
  R2 = Resistor [tolerance=±5% resistance=220 package=THT]
  S3 = Pushbutton [package="[THT]"]
  S4 = Pushbutton [package="[THT]"]
  S5 = Pushbutton [package="[THT]"]
  S6 = Pushbutton [package="[THT]"]
  R3 = Resistor [tolerance=±5% resistance=220 package=THT]
  R4 = Resistor [tolerance=±5% resistance=220 package=THT]
  R5 = Resistor [tolerance=±5% resistance=220 package=THT]
  R6 = Resistor [tolerance=±5% resistance=220 package=THT]
  IC6 = IC, DIP package, 18 pins [chip_label=IC74157]
  IC7 = IC, DIP package, 16 pins [chip_label=IC74173]
  IC8 = IC, DIP package, 14 pins [chip_label=IC7404]

nets:
  N1: Power_plug1.GND, S1.Pin_1, S1.Pin_2, S2.Pin_1, S2.Pin_2, S3.Pin_1, S3.Pin_2, S4.Pin_1, S4.Pin_2, S5.Pin_1, S5.Pin_2, S6.Pin_1, S6.Pin_2, IC6.pin9, IC7.pin1, IC7.pin2, IC7.pin8, IC7.pin9, IC7.pin10, IC7.pin15, IC8.pin7
  N2: Power_plug1.VCC, R1.Pin_0, R2.Pin_0, R3.Pin_0, R4.Pin_0, R5.Pin_0, R6.Pin_0, IC6.pin18, IC7.pin16, IC8.pin14
  N3: S1.Pin_3, S1.Pin_4, R1.Pin_1, IC6.pin1
  N4: S2.Pin_3, S2.Pin_4, R2.Pin_1, IC6.pin2
  N5: S3.Pin_3, S3.Pin_4, R3.Pin_1, IC6.pin5
  N6: S4.Pin_3, S4.Pin_4
  N7: S5.Pin_3, S5.Pin_4, R5.Pin_1, IC6.pin13
  N8: S6.Pin_3, S6.Pin_4, R6.Pin_1, IC6.pin12
  N9: R4.Pin_1, IC6.pin16
  N10: IC6.pin3, IC7.pin3
  N11: IC6.pin4, IC7.pin14
  N12: IC6.pin6, IC7.pin4
  N13: IC6.pin7, IC7.pin13
  N14: IC6.pin10, IC8.pin12
  N15: IC6.pin11, IC7.pin6
  N16: IC6.pin14, IC7.pin12
  N17: IC6.pin15, IC7.pin5
  N18: IC7.pin11, IC8.pin13

notes:
  e="PCB View" rect="30.1 -22.9 37.8 64.8"/>
  <boundingRect name="Schematic View" rect="17.5 -26.5 63 72"/
  </boundingRects>
  <instances>
  <instance modelIndex="85423793" moduleIdRef="generic_ic_dip_14_300mil" path="C:/Users/ARTA PC/AppData/Roaming/Fritzing/partfactory/aeaec5d69f44a894a713866c60d4c8f5/core/generic_ic_dip_14_300mil.fzp">
  <property name="chip label" value="IC7404"/>
  <title>IC6</title>
  <views>
  <schematicView layer="schematic">
  <geometry x="17.5" z="2.50002" y="-26.5"/>
  <titleGeometry textColor="#000000" x="80.5" z="7.00087" xOffset="63" fontSize="5" visible="true" y="-33.5" yOffset="-7">
  <displayKey key=""/>
  <displayKey key="part number"/>
  </titleGeometry>
  </schematicView>
  <breadboardView layer="breadboard">
  <geometry x="218.4" z="2.50002" y="-4.45"/>
  </breadboardView>
  <pcbView layer="copper0">
  <geometry x="30.1" z="5.50002" y="-22.9"/>
  <titleGeometry textColor="#000000" x="67.9" z="13.0009" xOffset="37.8" fontSize="5" visible="true" y="-29.9" yOffset="-7">
  <displayKey key=""/>
  </titleGeometry>
  </pcbView>
  </views>
  </instance>
  </instances>
  </module>
