# Fritzing sketch h (saved by Fritzing 0.9.4)
breadboards: 1

parts:
  IC1 = IC, DIP package, 14 pins [chip_label=IC7495]
  Power_plug1 = Power plug

nets:
  N1: IC1.pin6, IC1.pin7, Power_plug1.GND
  N2: IC1.pin14, Power_plug1.VCC

notes:
  clk
  inABCD
