# Fritzing sketch i (saved by Fritzing 0.9.4)
breadboards: 1

parts:
  IC1 = IC, DIP package, 14 pins [chip_label=IC7495]
  Power_plug1 = Power plug
  IC2 = IC, DIP package, 24 pins [chip_label=IC74154]
  IC3 = IC, DIP package, 14 pins [chip_label=IC7432(or)]

nets:
  N1: IC1.pin6, IC1.pin7, Power_plug1.GND
  N2: IC1.pin10, IC2.pin20
  N3: IC1.pin11, IC2.pin21
  N4: IC1.pin12, IC2.pin22
  N5: IC1.pin13, IC2.pin23
  N6: IC1.pin14, Power_plug1.VCC, IC2.pin24, IC3.pin14
  N7: IC2.pin2, IC3.pin1
  N8: IC2.pin3, IC3.pin2
  N9: IC2.pin12, IC3.pin7
  N10: IC2.pin15, IC3.pin13
  N11: IC2.pin16, IC3.pin12
  N12: IC3.pin3, IC3.pin4
  N13: IC3.pin5, IC3.pin11

notes:
  clk
  inABCD
