# Fritzing sketch a_main (saved by Fritzing 0.9.4)
breadboards: 1

parts:
  Power_plug1 = Power plug
  IC4 = IC, DIP package, 16 pins [chip_label=74153]
  IC5 = IC, DIP package, 16 pins [chip_label=74153]
  IC6 = IC, DIP package, 16 pins [chip_label=74173]

nets:
  N1: Power_plug1.GND, IC4.pin8, IC5.pin8, IC6.pin8
  N2: Power_plug1.VCC, IC4.pin16, IC5.pin16, IC6.pin16
  N3: IC4.pin7, IC6.pin14
  N4: IC4.pin9, IC6.pin13
  N5: IC4.pin10, IC6.pin3
  N6: IC4.pin14, IC5.pin14
  N7: IC5.pin6, IC6.pin4
  N8: IC5.pin7, IC6.pin12
  N9: IC5.pin9, IC6.pin11
  N10: IC5.pin10, IC6.pin5

notes:
  clk
  in0
  in3
  in2
  in1
  se
  pe
