# Fritzing sketch 5_1 (saved by Fritzing 0.9.4)
breadboards: 3

parts:
  74LS1 = 74LS76 [package="DIP (Dual Inline) [THT]"]
  74LS4 = 74LS76 [package="DIP (Dual Inline) [THT]"]
  U2 = 555 Timer [package="SO8 [SMD]"]  # not connected
  C2 = Capacitor [package=cap-pth-large]
  R2 = Resistor [tolerance=±5% resistance=220 package="1206 [SMD]"]
  VCC2 = Battery
  74LS5 = 74LS04 [package="DIP (Dual Inline) [THT]"]
  U3 = 4077 4 x 2 Input XNOR Gate, single part [part_number=4077 package="DIP (Dual Inline) [THT]"]

nets:
  N1: 74LS1.CLK1, 74LS5.2Y
  VCC: 74LS1.J1, 74LS1.J2, 74LS1.K2, 74LS1.K1, 74LS4.J1, 74LS4.J2, 74LS4.K2, 74LS4.K1, R2.Pin_1, VCC2.+, 74LS5.Vcc, U3.VDD
  N2: 74LS1.CLK2, U3.Q1
  N3: 74LS1.Q2, U3.A2
  N4: 74LS1.Q1, U3.B1
  N5: 74LS4.CLK1, U3.Q2
  N6: 74LS4.CLK2, U3.Q3
  N7: 74LS4.Q1, U3.B3
  GND: C2.2, VCC2.-, 74LS5.GND, U3.GND
  N8: U3.A1, U3.B2, U3.A3

notes:
  اگر ورودی کاربر را I بنامیم:
  ورودی کلاک فلیپ فلاپ بعدی برابر است با:(طبق پروتئوس)
  I XNOR Q
  بنابراین در اینحا با پیاده سازی ساده شده مدار اصلی کار خواهیم کرد.

custom parts:
  74LS76: The SN74LS76A offers individual J, K, Clock Pulse, Direct Set and Direct Clear inputs. These dual flip-flops are designed so that when the clock goes HIGH, the inputs are enabled and data will be accepted. The Logic Level of the J and K inputs will perform according to the Truth Table as long as minimum set-up times are observed. Input data is transferred to the outputs on the HIGH-to-LOW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
  74LS04: Hex Inverting Gates
