# Fritzing sketch 5_2 (saved by Fritzing 0.9.4)
breadboards: 4

parts:
  74LS1 = 74LS76 [package="DIP (Dual Inline) [THT]"]
  74LS4 = 74LS76 [package="DIP (Dual Inline) [THT]"]
  U2 = 555 Timer [package="SO8 [SMD]"]  # not connected
  C2 = Capacitor [package=cap-pth-large]
  R2 = Resistor [tolerance=±5% resistance=220 package="1206 [SMD]"]
  VCC2 = Battery
  74LS5 = 74LS04 [package="DIP (Dual Inline) [THT]"]
  U3 = 4077 4 x 2 Input XNOR Gate, single part [part_number=4077 package="DIP (Dual Inline) [THT]"]
  74LS6 = 74LS00 [package="DIP (Dual Inline) [THT]"]
  74LS7 = 74LS04 [package="DIP (Dual Inline) [THT]"]
  74LS8 = 74LS00 [package="DIP (Dual Inline) [THT]"]

nets:
  N1: 74LS1.CLK1, 74LS5.2Y
  N2: 74LS1.PRE1, 74LS6.4Y
  N3: 74LS1.CLR1, 74LS6.3Y
  VCC: 74LS1.J1, 74LS1.VCC, 74LS1.J2, 74LS1.K2, 74LS1.K1, 74LS4.J1, 74LS4.VCC, 74LS4.J2, 74LS4.K2, 74LS4.K1, R2.Pin_1, VCC2.+, 74LS5.Vcc, U3.VDD, 74LS6.Vcc, 74LS7.Vcc, 74LS8.Vcc
  N4: 74LS1.CLK2, U3.Q1
  N5: 74LS1.PRE2, 74LS6.1Y
  N6: 74LS1.CLR2, 74LS6.2Y
  N7: 74LS1.Q2, U3.A2
  N8: 74LS1.Q1, U3.B1
  N9: 74LS4.CLK1, U3.Q2
  N10: 74LS4.PRE1, 74LS8.4Y
  N11: 74LS4.CLR1, 74LS8.3Y
  N12: 74LS4.CLK2, U3.Q3
  N13: 74LS4.PRE2, 74LS8.1Y
  N14: 74LS4.CLR2, 74LS8.2Y
  N15: 74LS4.Q1, U3.B3
  GND: C2.2, VCC2.-, 74LS5.GND, U3.GND, 74LS6.GND, 74LS7.GND, 74LS8.GND
  N16: U3.A1, U3.B2, U3.A3
  N17: 74LS6.1A, 74LS6.2A, 74LS6.3B, 74LS6.4B, 74LS8.1A, 74LS8.2A, 74LS8.3B, 74LS8.4B
  N18: 74LS6.1B, 74LS7.1A
  N19: 74LS6.2B, 74LS7.1Y
  N20: 74LS6.3A, 74LS7.6Y
  N21: 74LS6.4A, 74LS7.6A
  N22: 74LS7.3A, 74LS8.1B, 74LS8.2B
  N23: 74LS7.5Y, 74LS8.3A
  N24: 74LS7.5A, 74LS8.4A

notes:
  اگر ورودی کاربر را I بنامیم:
  ورودی کلاک فلیپ فلاپ بعدی برابر است با:(طبق پروتئوس)
  I XNOR Q
  بنابراین در اینحا با پیاده سازی ساده شده مدار اصلی کار خواهیم کرد.

custom parts:
  74LS76: The SN74LS76A offers individual J, K, Clock Pulse, Direct Set and Direct Clear inputs. These dual flip-flops are designed so that when the clock goes HIGH, the inputs are enabled and data will be accepted. The Logic Level of the J and K inputs will perform according to the Truth Table as long as minimum set-up times are observed. Input data is transferred to the outputs on the HIGH-to-LOW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
  74LS04: Hex Inverting Gates
  74LS00: Quad 2-Input NAND Gate
