# Fritzing sketch 6 (saved by Fritzing 0.9.4)
breadboards: 3

parts:
  VCC1 = Battery
  74LS1 = 74LS08 [package="DIP (Dual Inline) [THT]"]
  74LS2 = 74LS00 [package="DIP (Dual Inline) [THT]"]
  IC1 = 74LS393N [part_number=DM74LS393N package=dil14]
  74LS3 = 74LS138 [package="DIP (Dual Inline) [THT]"]
  74LS4 = 74LS138 [package="DIP (Dual Inline) [THT]"]
  74LS5 = 74LS157 [package="DIP (Dual Inline) [THT]"]
  74LS6 = 74LS76 [package="DIP (Dual Inline) [THT]"]
  74LS7 = 74LS76 [package="DIP (Dual Inline) [THT]"]
  74LS8 = 74LS00 [package="DIP (Dual Inline) [THT]"]
  74LS9 = 74LS04 [package="DIP (Dual Inline) [THT]"]
  R1 = Resistor [tolerance=±5% resistance=220 package="0603 [SMD]"]
  R2 = Resistor [tolerance=±5% resistance=220 package="0603 [SMD]"]
  R3 = Resistor [tolerance=±5% resistance=220 package="0603 [SMD]"]
  R4 = Resistor [tolerance=±5% resistance=220 package="0603 [SMD]"]
  R5 = Resistor [tolerance=±5% resistance=220 package="0603 [SMD]"]
  LED1 = smd LED [color="Red (633nm)" package="0805 [SMD]"]
  LED2 = smd LED [color="Red (633nm)" package="0805 [SMD]"]
  LED3 = smd LED [color="Red (633nm)" package="0805 [SMD]"]
  LED4 = smd LED [color="Red (633nm)" package="0805 [SMD]"]
  LED5 = smd LED [color="Red (633nm)" package="0805 [SMD]"]

nets:
  GND: VCC1.-, 74LS1.GND, 74LS2.GND, IC1.P_GND, 74LS3.G2A', 74LS3.GND, 74LS4.G2A', 74LS4.G2B', 74LS4.GND, 74LS5.GND, 74LS5.G', 74LS6.CLR2, 74LS7.CLR2, 74LS8.GND, 74LS9.GND, LED1.cathode, LED2.cathode, LED3.cathode, LED4.cathode, LED5.cathode
  VCC: VCC1.+, 74LS1.Vcc, 74LS2.Vcc, IC1.P_VCC, 74LS3.G1, 74LS3.Vcc, 74LS4.Vcc, 74LS5.Vcc, 74LS6.K1, 74LS7.K1, 74LS8.Vcc, 74LS9.Vcc
  N1: 74LS1.1Y, 74LS2.1A
  N2: 74LS1.2Y, 74LS2.1B
  N3: 74LS2.1Y, IC1.A_CLR
  N4: IC1.A_QA, 74LS3.A, 74LS4.A
  N5: IC1.A_QB, 74LS3.B, 74LS4.B
  N6: IC1.A_QC, 74LS3.C, 74LS4.C
  N7: IC1.A_QD, 74LS3.G2B', 74LS4.G1
  N8: 74LS3.Y7', 74LS5.3A
  N9: 74LS3.Y5', 74LS5.1B, 74LS5.2A, 74LS8.4Y
  N10: 74LS3.Y2', 74LS5.1A, 74LS6.Q1', 74LS8.4B
  N11: 74LS3.Y0', 74LS6.Q1
  N12: 74LS4.Y4', 74LS5.4B, 74LS7.Q2'
  N13: 74LS4.Y2', 74LS5.3B
  N14: 74LS4.Y1', 74LS5.4A
  N15: 74LS4.Y0', 74LS5.2B
  N16: 74LS5.A'/B, 74LS9.1Y, 74LS9.3A
  N17: 74LS5.1Y, 74LS6.CLK2
  N18: 74LS5.2Y, 74LS6.VCC, 74LS7.Q1
  N19: 74LS5.3Y, 74LS7.Q2, 74LS7.Q1'
  N20: 74LS6.PRE2, R4.Pin_0
  N21: 74LS6.J2, R3.Pin_0
  N22: 74LS6.Q2', 74LS9.3Y
  N23: 74LS6.Q2, 74LS9.2A
  N24: 74LS6.GND, R2.Pin_0
  N25: 74LS7.J2, R1.Pin_0
  N26: 74LS7.GND, R5.Pin_0
  N27: 74LS8.3B, 74LS9.2Y
  N28: 74LS8.4A, 74LS9.1A
  N29: R1.Pin_1, LED5.anode
  N30: R2.Pin_1, LED1.anode
  N31: R3.Pin_1, LED2.anode
  N32: R4.Pin_1, LED3.anode
  N33: R5.Pin_1, LED4.anode

notes:
  Clock pulse from the generator
  Start Water Door Mode
  74279
  Hot?

custom parts:
  74LS08: Quad 2-Input AND Gates
  74LS00: Quad 2-Input NAND Gate
  74LS393N: Dual 4-bit decade and binary COUNTER
  74LS138: DM74LS138 3-to-8-line decoders incorporates 3 enable inputs to simplify cascading and/or data reception
  74LS157: Quad 2/1 Data Selector
  74LS76: The SN74LS76A offers individual J, K, Clock Pulse, Direct Set and Direct Clear inputs. These dual flip-flops are designed so that when the clock goes HIGH, the inputs are enabled and data will be accepted. The Logic Level of the J and K inputs will perform according to the Truth Table as long as minimum set-up times are observed. Input data is transferred to the outputs on the HIGH-to-LOW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
  74LS04: Hex Inverting Gates
